// Logisim project l02_decoder.circ as structural Verilog: 1 circuit, main circuit main
module main (
  input  A,
  input  B,
  input  C,
  output out_4,
  output Y1,
  output Y2,
  output Y3,
  output out_8,
  output Y5,
  output Y6,
  output out_11
);

  wire not_1_out, not_2_out, not_3_out;

  not not_1 (not_1_out, A);
  not not_2 (not_2_out, B);
  not not_3 (not_3_out, C);
  and and_1 (out_4, not_1_out, not_2_out, not_3_out);
  and and_2 (Y1, not_1_out, not_2_out, C);
  and and_3 (Y2, not_1_out, B, not_3_out);
  and and_4 (Y3, not_1_out, B, C);
  and and_5 (out_8, A, not_2_out, not_3_out);
  and and_6 (Y5, A, not_2_out, C);
  and and_7 (Y6, A, B, not_3_out);
  and and_8 (out_11, A, B, C);

  // Notes on the sheet:
  //   Y0
  //   Y4
  //   Y7
endmodule
